# Fritzing sketch circuit (saved by Fritzing 0.9.3b)
breadboards: 1

parts:
  Onderdeel1 = Arduino Due (Rev2b)
  R1 = Resistor [tolerance=±5% resistance=220 package="1206 [SMD]"]
  LED1 = LED - 3mm [color="Red (633nm)" package="3 mm [THT]"]

nets:
  N1: Onderdeel1.D13_PWM, R1.Pin_0
  N2: Onderdeel1.GND, LED1.anode
  N3: R1.Pin_1, LED1.cathode
